// Logisim project test.circ as structural Verilog: 1 circuit, main circuit main
module main (
);

  wire and_1_out, and_2_out, and_3_out, and_4_out, and_5_out, and_6_out, and_7_out, and_8_out, and_9_out,
       and_10_out, and_11_out, and_12_out, and_13_out, clock_1_out, clock_2_out, clock_3_out, clock_4_out,
       clock_5_out, clock_6_out, clock_7_out, clock_8_out, comparator_1_eq, comparator_2_eq, comparator_3_eq,
       comparator_4_gt, comparator_5_lt, comparator_6_eq, comparator_7_eq, comparator_8_eq, comparator_9_eq,
       comparator_10_eq, comparator_11_eq, keyboard_1_avail, keyboard_2_avail, rv32im_cpu_1_p2,
       rv32im_cpu_1_p5, rv32im_cpu_1_p6, rv32im_cpu_1_p7, rv32im_cpu_1_p8, rv32im_cpu_1_p9, rv32im_cpu_1_p10,
       rv32im_cpu_1_p11;
  wire [6:0] keyboard_1_data, keyboard_2_data;
  wire [31:0] bit_extender_1_out, bit_extender_2_out, bit_extender_3_out, bit_extender_4_out, rom_1_data,
       rv32im_cpu_1_p3, rv32im_cpu_1_p4;

  Clock clock_1 (.out(clock_1_out));
  // RV32IM_CPU #(.hexRegisters("true")) rv32im_cpu_1: pin names not known; wires that end beside it: clock_1_out, rv32im_cpu_1_p2, rv32im_cpu_1_p3, rv32im_cpu_1_p4, rv32im_cpu_1_p5, rv32im_cpu_1_p6, rv32im_cpu_1_p7, rv32im_cpu_1_p8, rv32im_cpu_1_p9, rv32im_cpu_1_p10, rv32im_cpu_1_p11
  Pull_Resistor pull_resistor_1 (.node(rv32im_cpu_1_p5));
  Pull_Resistor pull_resistor_2 (.node(rv32im_cpu_1_p6));
  Pull_Resistor pull_resistor_3 ();  // open: node
  and and_1 (and_1_out, rv32im_cpu_1_p6, and_4_out);
  and and_2 (and_2_out, and_4_out, rv32im_cpu_1_p5);
  RAM #(.addrWidth(14), .asyncread("true"), .byteenables("byteEnables"), .dataWidth(32), .databus("bidir")) ram_1 (
    .addr(rv32im_cpu_1_p3[15:2]), .we(and_1_out), .oe(and_2_out), .clk(clock_2_out), .data(rv32im_cpu_1_p4),
    .be3(rv32im_cpu_1_p11), .be2(rv32im_cpu_1_p10), .be1(rv32im_cpu_1_p9), .be0(rv32im_cpu_1_p8));
  Clock clock_2 (.out(clock_2_out));
  Comparator #(.width(32)) comparator_1 (.a(rv32im_cpu_1_p3), .b(32'hfff00000), .eq(comparator_1_eq));  // open: gt, lt
  Comparator #(.width(16)) comparator_2 (
    .a(rv32im_cpu_1_p3[31:16]), .b({16{1'b0}}), .eq(comparator_2_eq));  // open: gt, lt
  Comparator #(.width(16)) comparator_3 (.a(rv32im_cpu_1_p3[31:16]), .b(16'h11), .eq(comparator_3_eq));  // open: gt, lt
  Comparator #(.width(16)) comparator_4 (
    .a(rv32im_cpu_1_p3[31:16]), .b({16{1'b0}}), .gt(comparator_4_gt));  // open: eq, lt
  and and_3 (and_3_out, rv32im_cpu_1_p5, comparator_2_eq);
  Comparator #(.width(16)) comparator_5 (.a(rv32im_cpu_1_p3[31:16]), .b(16'h3), .lt(comparator_5_lt));  // open: gt, eq
  Pull_Resistor pull_resistor_4 (.node(comparator_5_lt));
  and and_4 (and_4_out, comparator_5_lt, comparator_4_gt);
  ROM #(.addrWidth(14), .dataWidth(32)) rom_1 (.addr(rv32im_cpu_1_p3[15:2]), .data(rom_1_data));
  Clock clock_3 (.out(clock_3_out));
  and and_5 (and_5_out, rv32im_cpu_1_p6, comparator_1_eq);
  TTY #(.cols(100), .rows(40)) tty_1 (.data(rv32im_cpu_1_p4[6:0]), .clk(clock_3_out), .we(and_5_out));  // open: clr
  assign rv32im_cpu_1_p4 = and_3_out ? rom_1_data : 32'bz;  // Controlled_Buffer controlled_buffer_1
  and and_6 (and_6_out, rv32im_cpu_1_p5, comparator_3_eq);
  and and_7 (and_7_out, rv32im_cpu_1_p6, comparator_3_eq);
  Clock clock_4 (.out(clock_4_out));
  Comparator #(.width(32)) comparator_6 (.a(rv32im_cpu_1_p3), .b(32'hfff00100), .eq(comparator_6_eq));  // open: gt, lt
  Comparator #(.width(32)) comparator_7 (.a(rv32im_cpu_1_p3), .b(32'hfff00200), .eq(comparator_7_eq));  // open: gt, lt
  Comparator #(.width(32)) comparator_8 (.a(rv32im_cpu_1_p3), .b(32'hfff00104), .eq(comparator_8_eq));  // open: gt, lt
  Comparator #(.width(32)) comparator_9 (.a(rv32im_cpu_1_p3), .b(32'hfff00204), .eq(comparator_9_eq));  // open: gt, lt
  // Hard_Drive_DMA #(.file_name("circuits\\testFileSystem\\hard_drive.bin")) hard_drive_dma_1: pin names not known; wires that end beside it: rv32im_cpu_1_p3, and_6_out, and_7_out, rv32im_cpu_1_p11, rv32im_cpu_1_p10, rv32im_cpu_1_p9, rv32im_cpu_1_p8, rv32im_cpu_1_p7, clock_4_out, rv32im_cpu_1_p4, rv32im_cpu_1_p5, rv32im_cpu_1_p6, rv32im_cpu_1_p3, rv32im_cpu_1_p2
  Clock clock_5 (.out(clock_5_out));
  Keyboard keyboard_1 (
    .clk(clock_5_out), .re(and_8_out), .avail(keyboard_1_avail), .data(keyboard_1_data));  // open: clr
  and and_8 (and_8_out, comparator_6_eq, rv32im_cpu_1_p5);
  and and_9 (and_9_out, comparator_7_eq, rv32im_cpu_1_p5);
  Clock clock_6 (.out(clock_6_out));
  Keyboard keyboard_2 (
    .clk(clock_6_out), .re(and_10_out), .avail(keyboard_2_avail), .data(keyboard_2_data));  // open: clr
  and and_10 (and_10_out, comparator_8_eq, rv32im_cpu_1_p5);
  and and_11 (and_11_out, comparator_9_eq, rv32im_cpu_1_p5);
  assign bit_extender_1_out = {{25{1'b0}}, keyboard_1_data};  // Bit_Extender bit_extender_1
  assign rv32im_cpu_1_p4 = and_8_out ? bit_extender_1_out : 32'bz;  // Controlled_Buffer controlled_buffer_2
  assign bit_extender_2_out = {{31{1'b0}}, keyboard_1_avail};  // Bit_Extender bit_extender_2
  assign rv32im_cpu_1_p4 = and_9_out ? bit_extender_2_out : 32'bz;  // Controlled_Buffer controlled_buffer_3
  assign bit_extender_3_out = {{25{1'b0}}, keyboard_2_data};  // Bit_Extender bit_extender_3
  assign rv32im_cpu_1_p4 = and_10_out ? bit_extender_3_out : 32'bz;  // Controlled_Buffer controlled_buffer_4
  assign bit_extender_4_out = {{31{1'b0}}, keyboard_2_avail};  // Bit_Extender bit_extender_4
  assign rv32im_cpu_1_p4 = and_11_out ? bit_extender_4_out : 32'bz;  // Controlled_Buffer controlled_buffer_5
  TTY #(.cols(100), .rows(40)) tty_2 (.data(rv32im_cpu_1_p4[6:0]), .clk(clock_7_out), .we(and_12_out));  // open: clr
  Clock clock_7 (.out(clock_7_out));
  Clock clock_8 (.out(clock_8_out));
  TTY tty_3 (.data(rv32im_cpu_1_p4[6:0]), .clk(clock_8_out), .we(and_13_out));  // open: clr
  Comparator #(.width(32)) comparator_10 (
    .a(rv32im_cpu_1_p3), .b(32'hfff00004), .eq(comparator_10_eq));  // open: gt, lt
  and and_12 (and_12_out, comparator_10_eq, rv32im_cpu_1_p6);
  Comparator #(.width(32)) comparator_11 (
    .a(rv32im_cpu_1_p3), .b(32'hfff00008), .eq(comparator_11_eq));  // open: gt, lt
  and and_13 (and_13_out, comparator_11_eq, rv32im_cpu_1_p6);

  // Notes on the sheet:
  //   contents of rom_1 (hex, n*v repeats v):
  //   1b117 ffc10113 513 593 613 20d010ef 6f fc010113 2112e23 2812c23 4010413 50793 fcf407a3 87b7 45478793
  //   7a583 47a603 87a683 c7a703 fcb42e23 fec42023 fed42223 fee42423 107c783 fef40623 fcf44783 47d793
  //   ff7f793 f7f793 ff040713 f707b3 fec7c783 fcf40c23 fcf44783 f7f793 ff040713 f707b3 fec7c783 fcf40ca3
  //   fc040d23 fd840793 78513 471010ef 13 3c12083 3812403 4010113 8067 dc010113 22112e23 22812c23 24010413
  //   dca42623 dcb42423 87b7 46878513 439010ef 593 dcc42503 714030ef fea42023 107b7 9078693 fe042703 70793
  //   179793 e787b3 279793 f687b3 7a023 fe042623 dc842783 fef42423 87b7 48878513 3ed010ef dc842783 78513
  //   34d010ef 800006f fdc42703 ddc40793 70613 78593 fe842503 84070ef fdc42783 fe842703 f707b3 fef42423
  //   fec42703 fdc42783 f707b3 fef42623 87b7 4a878513 399010ef fdc42503 2fd010ef 87b7 4b078513 385010ef
  //   fdc42783 40f007b3 fe842703 f707b3 78513 2d9010ef 87b7 4c478513 361010ef ddc40793 20000613 78593
  //   fe042503 8c040ef fca42e23 fdc42783 f6f044e3 fe042503 bd040ef 87b7 4c878513 32d010ef fec42503
  //   291010ef 87b7 4c478513 319010ef 87b7 4f478513 30d010ef fe042223 340006f fe442703 dc842783 f707b3
  //   7c783 78513 df1ff0ef 87b7 50c78513 2e1010ef fe442783 178793 fef42223 fe442703 f00793 e7c863 fe442703
  //   fec42783 faf74ee3 87b7 4c478513 2b1010ef fec42783 78513 23c12083 23812403 24010113 8067 ff010113
  //   112623 812423 1010413 200593 87b7 51078513 560030ef 50793 7dc63 613 100593 87b7 51078513 2f4060ef
  //   200593 87b7 51c78513 534030ef 50793 7dc63 100613 100593 87b7 51c78513 2c8060ef 13 c12083 812403
  //   1010113 8067 fe010113 112e23 812c23 2010413 1b5b7 87b7 52878513 da5ff0ef fea42623 fec42783 f04c63
  //   87b7 53078513 1e5010ef fff00793 1180006f 87b7 54878513 1d1010ef fec42503 135010ef 87b7 4c478513
  //   1bd010ef 9000613 593 107b7 78513 571060ef 10793 fef42423 107b7 78793 fe842703 e7a223 107b7 78793
  //   1b737 e7a623 107b7 78793 1f737 e7ac23 77b7 7f878713 107b7 78793 e7a423 87b7 56c78513 151010ef 107b7
  //   78793 c7a783 78513 a9010ef 87b7 4c478513 131010ef 87b7 58478513 125010ef 107b7 78793 187a783 78513
  //   7d010ef 87b7 4c478513 105010ef 87b7 59c78513 f9010ef 107b7 78793 87a783 78513 51010ef 87b7 4c478513
  //   d9010ef 107b7 78793 7a023 793 78513 1c12083 1812403 2010113 8067 f9010113 6112623 6812423 7010413
  //   87b7 5b878513 5a1070ef fe042623 1ac0006f fec42503 3e5070ef 50793 2079463 87b7 5dc78513 57d070ef
  //   fec42503 5c1070ef 87b7 5e878513 569070ef 16c0006f 87b7 60478513 559070ef fec42503 59d070ef 87b7
  //   61878513 545070ef 87b7 5dc78793 fef42023 fe042423 300006f fe842783 fe042703 f707b3 7c703 fe842783
  //   ff040693 f687b3 fae78623 fe842783 178793 fef42423 fe842783 fe042703 f707b3 7c783 78863 fe842703
  //   3500793 fae7dce3 fec42783 ff7f713 fe842783 178693 fed42423 3070713 ff77713 ff040693 f687b3 fae78623
  //   fe842783 178713 fee42423 ff040713 f707b3 3a00713 fae78623 fe842783 178713 fee42423 ff040713 f707b3
  //   2000713 fae78623 87b7 62078793 fcf42e23 fe042223 380006f fe442783 178713 fee42223 78713 fdc42783
  //   e78733 fe842783 178693 fed42423 74703 ff040693 f687b3 fae78623 fe442783 fdc42703 f707b3 7c783 78863
  //   fe842703 3e00793 fae7d8e3 fe842783 ff040713 f707b3 fa078623 f9c40793 78593 fec42503 70c070ef
  //   fec42783 178793 fef42623 fec42703 100793 e4e7d8e3 87b7 63478513 3d9070ef 13 6c12083 6812403 7010113
  //   8067 dd010113 22112623 22812423 23010413 87b7 65878593 100513 4c8060ef 87b7 67478513 518060ef 50793
  //   79c63 87b7 68078593 100513 4a4060ef 140006f 87b7 69878593 100513 490060ef 87b7 67478513 5ac060ef
  //   50793 79c63 87b7 6a878593 100513 46c060ef 140006f 87b7 6c078593 100513 458060ef ed840793 10000593
  //   78513 5b4060ef 87b7 6d078593 100513 438060ef ed840793 78593 100513 428060ef 87b7 4c478593 100513
  //   418060ef d00593 87b7 6d878513 2d0060ef fea42423 fe842783 407c463 87b7 6ec78793 fef42223 fe442503
  //   7a8060ef 50793 78613 fe442583 fe842503 378060ef fe842503 2e0060ef 87b7 70878593 100513 3bc060ef
  //   140006f 87b7 72478593 100513 3a8060ef 593 87b7 6d878513 260060ef fea42423 fe842783 407ca63 dd840793
  //   3f00613 78593 fe842503 2c0060ef fea42023 fe042783 ff040713 f707b3 de078423 87b7 73878593 100513
  //   354060ef dd840793 78593 100513 344060ef fe842503 250060ef 593 87b7 67478513 1f4060ef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
endmodule
