// Logisim project test_modified_RAM.circ as structural Verilog: 1 circuit, main circuit main
module main (
);

  wire and_1_out, and_2_out, and_3_out, button_1_out, clock_1_out, clock_2_out, comparator_1_eq,
       comparator_2_eq, MemRead, MemWrite, or_1_out;
  wire [31:0] CPU1_p3, CPU1_p4, CPU1_p5, ram_1_dout, rom_1_data;

  Button button_1 (.out(button_1_out));
  Clock clock_1 (.out(clock_1_out));
  // rv_32_im #(.resetAddress('h400000)) CPU1: pin names not known; wires that end beside it: clock_1_out, button_1_out, CPU1_p3, CPU1_p4, CPU1_p5, MemRead, MemWrite
  Comparator #(.width(16)) comparator_1 (.a(CPU1_p4[31:16]), .b(16'h1001), .eq(comparator_1_eq));  // open: gt, lt
  Comparator #(.width(16)) comparator_2 (.a(CPU1_p4[31:16]), .b(16'h40), .eq(comparator_2_eq));  // open: gt, lt
  and and_1 (and_1_out, comparator_1_eq, MemWrite);
  Clock clock_2 (.out(clock_2_out));
  or or_1 (or_1_out, MemWrite, MemRead);
  ROM #(.addrWidth(14), .dataWidth(32)) rom_1 (.addr(CPU1_p4[15:2]), .data(rom_1_data));
  and and_2 (and_2_out, comparator_2_eq, MemRead);
  RAM #(.addrWidth(14), .asyncread("true"), .dataWidth(32)) ram_1 (
    .addr(CPU1_p4[15:2]), .we(and_1_out), .oe(1'b1), .clk(clock_2_out), .din(CPU1_p5), .dout(ram_1_dout));
  and and_3 (and_3_out, comparator_1_eq, or_1_out);
  assign CPU1_p3 = and_2_out ? rom_1_data : 32'bz;  // Controlled_Buffer controlled_buffer_1
  assign CPU1_p3 = and_3_out ? ram_1_dout : 32'bz;  // Controlled_Buffer controlled_buffer_2

  // Notes on the sheet:
  //   Data Out >>
  //   Address >>
  //   contents of rom_1 (hex, n*v repeats v):
  //   300093
  //   RAM
endmodule
