// Logisim project towers_test.circ as structural Verilog: 1 circuit, main circuit logisim_test_verif
module logisim_test_verif (
  output halt
);

  wire and_1_out, and_2_out, and_3_out, and_4_out, and_5_out, and_6_out, and_7_out, button_1_out,
       clock_1_out, clock_2_out, clock_3_out, clock_4_out, comparator_1_eq, comparator_2_eq, comparator_3_eq,
       comparator_4_eq, comparator_5_eq, comparator_6_eq, keyboard_1_avail, rv32im_cpu_1_p6, rv32im_cpu_1_p7,
       rv32im_cpu_1_p8, rv32im_cpu_1_p9;
  wire [6:0] keyboard_1_data;
  wire [31:0] bit_extender_1_out, bit_extender_2_out, counter_1_q, ram_1_dout, rom_1_data, rv32im_cpu_1_p3,
       rv32im_cpu_1_p4, rv32im_cpu_1_p5;

  Clock clock_1 (.out(clock_1_out));
  Button button_1 (.out(button_1_out));
  // RV32IM_CPU #(.gdbServerRunning("true"), .hexRegisters("true"), .resetAddress('h400000)) rv32im_cpu_1: pin names not known; wires that end beside it: clock_1_out, button_1_out, rv32im_cpu_1_p3, rv32im_cpu_1_p4, rv32im_cpu_1_p5, rv32im_cpu_1_p6, rv32im_cpu_1_p7, rv32im_cpu_1_p8, rv32im_cpu_1_p9
  not not_1 (halt, rv32im_cpu_1_p8);
  Button button_2 (.out(rv32im_cpu_1_p9));
  LED led_1 (.in(rv32im_cpu_1_p8));
  ROM #(.addrWidth(12), .dataWidth(32)) rom_1 (.addr(rv32im_cpu_1_p4[13:2]), .data(rom_1_data));
  Comparator #(.width(18)) comparator_1 (
    .a(rv32im_cpu_1_p4[31:14]), .b(18'h100), .eq(comparator_1_eq));  // open: gt, lt
  RAM #(.addrWidth(24), .asyncread("true"), .dataWidth(32)) ram_1 (
    .addr(rv32im_cpu_1_p4[25:2]), .we(and_1_out), .oe(1'b1), .clk(clock_2_out), .din(rv32im_cpu_1_p5),
    .dout(ram_1_dout));
  and and_1 (and_1_out, rv32im_cpu_1_p7, comparator_2_eq);
  Clock clock_2 (.out(clock_2_out));
  Comparator #(.width(6)) comparator_2 (
    .a(rv32im_cpu_1_p4[31:26]), .b(6'b100000), .eq(comparator_2_eq));  // open: gt, lt
  Clock clock_3 (.out(clock_3_out));
  Comparator #(.width(32)) comparator_3 (.a(rv32im_cpu_1_p4), .b(32'hffff000c), .eq(comparator_3_eq));  // open: gt, lt
  Comparator #(.width(32)) comparator_4 (.a(rv32im_cpu_1_p4), .b(32'hffff0008), .eq(comparator_4_eq));  // open: gt, lt
  Comparator #(.width(32)) comparator_5 (.a(rv32im_cpu_1_p4), .b(32'hffff0004), .eq(comparator_5_eq));  // open: gt, lt
  Comparator #(.width(32)) comparator_6 (.a(rv32im_cpu_1_p4), .b(32'hffff0020), .eq(comparator_6_eq));  // open: gt, lt
  and and_2 (and_2_out, comparator_1_eq, rv32im_cpu_1_p6);
  and and_3 (and_3_out, comparator_2_eq, rv32im_cpu_1_p6);
  TTY tty_1 (.data(rv32im_cpu_1_p5[6:0]), .clk(clock_3_out), .we(and_4_out));  // open: clr
  and and_4 (and_4_out, comparator_3_eq, rv32im_cpu_1_p7);
  Keyboard keyboard_1 (.avail(keyboard_1_avail), .data(keyboard_1_data));  // open: clk, re, clr
  and and_5 (and_5_out, comparator_4_eq, rv32im_cpu_1_p6);
  and and_6 (and_6_out, comparator_5_eq, rv32im_cpu_1_p6);
  and and_7 (and_7_out, comparator_6_eq, rv32im_cpu_1_p6);
  Clock clock_4 (.out(clock_4_out));
  assign rv32im_cpu_1_p3 = and_2_out ? rom_1_data : 32'bz;  // Controlled_Buffer controlled_buffer_1
  assign rv32im_cpu_1_p3 = and_3_out ? ram_1_dout : 32'bz;  // Controlled_Buffer controlled_buffer_2
  assign bit_extender_1_out = {{25{1'b0}}, keyboard_1_data};  // Bit_Extender bit_extender_1
  assign rv32im_cpu_1_p3 = and_5_out ? bit_extender_1_out : 32'bz;  // Controlled_Buffer controlled_buffer_3
  assign bit_extender_2_out = {{31{1'b0}}, keyboard_1_avail};  // Bit_Extender bit_extender_2
  assign rv32im_cpu_1_p3 = and_6_out ? bit_extender_2_out : 32'bz;  // Controlled_Buffer controlled_buffer_4
  assign rv32im_cpu_1_p3 = and_7_out ? counter_1_q : 32'bz;  // Controlled_Buffer controlled_buffer_5
  Counter #(.max('hffffffff), .width(32)) counter_1 (
    .Q(counter_1_q), .clk(clock_4_out));  // open: load, D, count, carry, up, clr

  // Notes on the sheet:
  //   contents of rom_1 (hex, n*v repeats v):
  //   83c00117 ffc10113 513 593 613 34c000ef 6f 54783 78e63 150513 ffff0737 f70623 150513 fff54783
  //   fe079ae3 8067 fe010113 112e23 410793 ffc10893 900813 3000593 5700313 180006f c70733 e783a3 40455513
  //   fff78793 1178c63 f57713 58613 fee852e3 30613 fddff06f 10623 410513 f8dff0ef 1c12083 2010113 8067
  //   52503 8067 52023 52223 8067 7fc00717 f9470713 472783 47a683 d72223 452703 e7a223 f52223 b7a023 52783
  //   178793 f52023 8067 50793 452703 72503 472683 d7a223 7fc00697 f4c68693 46a603 c72223 e6a223 7a703
  //   fff70713 e7a023 8067 ff010113 112623 812423 50413 52783 f05a63 40513 fadff0ef 42783 fef04ae3 c12083
  //   812403 1010113 8067 ff010113 112623 812423 912223 58413 b52023 52223 850493 52423 52623 52823 52a23
  //   52c23 52e23 b05c63 40593 48513 f19ff0ef fff40413 fe0418e3 c12083 812403 412483 1010113 8067 ff010113
  //   112623 812423 50413 850513 f51ff0ef 1040513 f49ff0ef 1840513 f41ff0ef 42583 40513 f6dff0ef c12083
  //   812403 1010113 8067 fe010113 112e23 812c23 912a23 1212823 1312623 1412423 50493 60913 70993 100793
  //   6f58663 68a13 fff58413 68713 98693 40593 fbdff0ef 98713 a0693 90613 100593 48513 fa5ff0ef 98713
  //   90693 a0613 40593 48513 f8dff0ef 1c12083 1812403 1412483 1012903 c12983 812a03 2010113 8067 60513
  //   e4dff0ef 50593 98513 e0dff0ef 44a783 178793 f4a223 fc1ff06f ff010113 112623 1850713 1050693 850613
  //   52583 f2dff0ef c12083 1010113 8067 50613 852783 4079a63 1052503 4051a63 62583 1862783 4f59863
  //   1c62783 78e63 50713 170713 7a683 4e69063 47a783 fe0798e3 100793 b795b3 fff58593 462783 2b78463
  //   600513 8067 200513 8067 300513 8067 400513 8067 500513 8067 fd010113 2112623 2812423 2912223 517
  //   10450513 ca5ff0ef 517 10c50513 c99ff0ef 900513 cb5ff0ef 517 10850513 c85ff0ef 7fc00717 cac70713
  //   7fc00797 c5c78793 f72223 900693 d72023 407a223 6300713 4e7a023 7fc00797 c4478793 713 800613 70693
  //   170713 fef7ae23 fed7ac23 878793 fec716e3 900593 10513 d65ff0ef 10513 dc1ff0ef 10513 eb9ff0ef 10513
  //   ed9ff0ef 50413 517 8850513 c01ff0ef 40513 c1dff0ef 517 7050513 bedff0ef ffff07b7 207a483 517 6c50513
  //   bd9ff0ef 48513 bf5ff0ef 517 4850513 bc5ff0ef 40513 2c12083 2812403 2412483 3010113 8067 65776f54
  //   6f207372 61482066 a696f6e 0 5f4d554e 43534944 203d2053 0 a 75736552 3d20746c 20 61746f54 6c43206c
  //   206b636f 6b636954 203d2073
endmodule
